// Digital circuit Final_NAND.dig as structural Verilog
module Final_NAND (
  input  R,
  input  B,
  input  S,
  input  E,
  output Energia,
  output IBB,
  output IRD,
  output IS,
  output _0_R___1_B
);

  wire nand_1_out, nand_2_out, nand_3_out, nand_4_out, not_1_out;

  not not_1 (not_1_out, R);
  nand nand_1 (nand_1_out, B, E);
  nand nand_2 (nand_2_out, E, R);
  nand nand_3 (nand_3_out, E, S);
  nand nand_4 (nand_4_out, B, not_1_out);
  not not_2 (IS, nand_3_out);
  not not_3 (_0_R___1_B, nand_4_out);
  nand nand_5 (Energia, nand_1_out, nand_2_out);

  assign IBB = B;
  assign IRD = R;
endmodule
